# Fritzing sketch ProjectLayout (saved by Fritzing 0.9.3b)
breadboards: 1

parts:
  Bauteil1 = Arduino Board Ethernet
  Bauteil2 = Arduino Nano (Rev3.0)
  Bauteil3 = 10-DOF IMU L3GD20H + LSM303 + BMP180 [part_number=1604]

nets:
  N1: Bauteil1.D10_PWM/SS, Bauteil2.D10
  N2: Bauteil2.RESET, Bauteil3.GND
  5V: Bauteil2.5V, Bauteil3.VIN
  N3: Bauteil2.A5, Bauteil3.SCL
  N4: Bauteil2.A4, Bauteil3.SDA

custom parts:
  10-DOF IMU L3GD20H + LSM303 + BMP180: This inertial-measurement-unit combines 3 of the best quality sensors available on the market to give you 11 axes of data: 3 axes of accelerometer data, 3 axes gyroscopic, 3 axes magnetic (compass), barometric pressure/altitude and temperature. We tested many different 'combination' sensors and found these were the best value, with stable and reliable readings.
